// Logisim project 8-bit sipo.circ as structural Verilog: 1 circuit, main circuit main
module main (
  input  SI,
  input  in_2,
  output out_3,
  output out_4,
  output out_5,
  output out_6,
  output out_7,
  output out_8,
  output out_9,
  output out_10
);

  wire clock_1_out, d_ff_1_qn, d_ff_2_qn, d_ff_3_qn, d_ff_4_qn, d_ff_5_qn, d_ff_6_qn;

  Clock clock_1 (.out(clock_1_out));
  D_Flip_Flop d_ff_1 (.clk(clock_1_out), .D(SI), .Q(out_3), .Qn(d_ff_1_qn), .preset(in_2));  // open: en, reset
  D_Flip_Flop d_ff_2 (.clk(clock_1_out), .D(d_ff_1_qn), .Q(out_4), .Qn(d_ff_2_qn), .preset(in_2));  // open: en, reset
  D_Flip_Flop d_ff_3 (.clk(clock_1_out), .D(d_ff_4_qn), .Q(out_6), .Qn(d_ff_3_qn), .preset(in_2));  // open: en, reset
  D_Flip_Flop d_ff_4 (.clk(clock_1_out), .D(d_ff_2_qn), .Q(out_5), .Qn(d_ff_4_qn), .preset(in_2));  // open: en, reset
  D_Flip_Flop d_ff_5 (.clk(clock_1_out), .D(d_ff_3_qn), .Q(out_7), .Qn(d_ff_5_qn), .preset(in_2));  // open: en, reset
  D_Flip_Flop d_ff_6 (.clk(clock_1_out), .D(d_ff_5_qn), .Q(out_8), .Qn(d_ff_6_qn), .preset(in_2));  // open: en, reset
  D_Flip_Flop d_ff_7 (.clk(clock_1_out), .D(d_ff_6_qn), .Q(out_9), .preset(in_2));  // open: Qn, en, reset
  D_Flip_Flop d_ff_8 (.clk(clock_1_out), .Q(out_10), .preset(in_2));  // open: D, Qn, en, reset
endmodule
