// Logisim project full adder.circ as structural Verilog: 1 circuit, main circuit main
module main (
  input  A,
  input  B,
  input  Cin,
  output X,
  output C1,
  output SUM,
  output Cout,
  output C2
);

  and AND (C1, A, B);
  xor XOR_2 (SUM, X, Cin);
  and AND_2 (C2, X, Cin);
  xor XOR (X, A, B);
  or OR (Cout, C1, C2);
endmodule
