// Logisim project half adder.circ as structural Verilog: 1 circuit, main circuit main
module main (
  input  A,
  input  B,
  output Sum,
  output Carry
);

  xor XOR (Sum, A, B);
  and AND (Carry, A, B);
endmodule
